// Logisim project Digital_ULA.circ as structural Verilog: 8 circuits, main circuit main
module main (
  input  A6,
  input  A,
  input  B,
  input  C,
  input  B6,
  input  A5,
  input  B5,
  input  A4,
  input  B4,
  input  A3,
  input  B3,
  input  A2,
  input  B2,
  input  A1,
  input  B1,
  input  A0,
  input  B0,
  output out_18,
  output out_19,
  output out_20,
  output out_21,
  output out_22,
  output out_23,
  output out_24,
  output out_25
);

  wire and_1_out, and_2_out, and_3_out, and_4_out, and_5_out, and_6_out, and_7_out, and_8_out, and_9_out,
       and_10_out, and_11_out, and_12_out, and_13_out, and_14_out, nor_1_out;

  nor nor_1 (nor_1_out, C, B, A);
  and and_1 (and_1_out, nor_1_out, A4);
  and and_2 (and_2_out, nor_1_out, A3);
  and and_3 (and_3_out, nor_1_out, A2);
  and and_4 (and_4_out, nor_1_out, A1);
  and and_5 (and_5_out, nor_1_out, A0);
  and and_6 (and_6_out, A6, nor_1_out);
  and and_7 (and_7_out, nor_1_out, A5);
  and and_8 (and_8_out, nor_1_out, B6);
  and and_9 (and_9_out, nor_1_out, B5);
  and and_10 (and_10_out, nor_1_out, B4);
  and and_11 (and_11_out, nor_1_out, B3);
  and and_12 (and_12_out, nor_1_out, B2);
  and and_13 (and_13_out, nor_1_out, B1);
  and and_14 (and_14_out, nor_1_out, B0);
  // Somador_de_8_bits somador_de_8_bits_1: pin names not known; wires that end beside it: and_6_out, and_8_out, and_7_out, and_9_out, and_1_out, and_10_out, and_2_out, and_11_out, and_3_out, and_12_out, and_4_out, and_13_out, and_5_out, and_14_out, out_18, out_19, out_20, out_21, out_22, out_23, out_24, out_25
endmodule

module Somador_de_1_bit (
  input  A,
  input  B,
  input  Carry_In,
  output Sum,
  output Carry_Out
);

  wire and_1_out, and_2_out, and_3_out, xor_1_out;

  and and_1 (and_1_out, B, A);
  and and_2 (and_2_out, B, Carry_In);
  and and_3 (and_3_out, A, Carry_In);
  xor xor_1 (xor_1_out, A, B);
  xor xor_2 (Sum, xor_1_out, Carry_In);
  or or_1 (Carry_Out, and_1_out, and_2_out, and_3_out);
endmodule

module Somador_de_8_bits (
  input  A4,
  input  A5,
  input  A3,
  input  B5,
  input  B4,
  input  B3,
  input  A6,
  input  B6,
  input  A2,
  input  B2,
  input  A1,
  input  A0,
  input  B1,
  input  B0,
  output out_15,
  output out_16,
  output out_17,
  output out_18,
  output out_19,
  output out_20,
  output out_21,
  output out_22
);

  wire not_1_out, somador_de_1_bit_1_carry_out, somador_de_1_bit_1_sum, somador_de_1_bit_2_carry_out,
       somador_de_1_bit_2_sum, somador_de_1_bit_3_carry_out, somador_de_1_bit_3_sum,
       somador_de_1_bit_4_carry_out, somador_de_1_bit_4_sum, somador_de_1_bit_5_carry_out,
       somador_de_1_bit_5_sum, somador_de_1_bit_6_carry_out, somador_de_1_bit_6_sum,
       somador_de_1_bit_7_carry_out, somador_de_1_bit_7_sum;

  Somador_de_1_bit somador_de_1_bit_1 (
    .A(A6), .B(B6), .Carry_In(1'b0), .Sum(somador_de_1_bit_1_sum), .Carry_Out(somador_de_1_bit_1_carry_out));
  Somador_de_1_bit somador_de_1_bit_2 (
    .A(A2), .B(B2), .Carry_In(somador_de_1_bit_7_carry_out), .Sum(somador_de_1_bit_2_sum),
    .Carry_Out(somador_de_1_bit_2_carry_out));
  Somador_de_1_bit somador_de_1_bit_3 (
    .A(A5), .B(B5), .Carry_In(somador_de_1_bit_1_carry_out), .Sum(somador_de_1_bit_3_sum),
    .Carry_Out(somador_de_1_bit_3_carry_out));
  Somador_de_1_bit somador_de_1_bit_4 (
    .A(A1), .B(B1), .Carry_In(somador_de_1_bit_2_carry_out), .Sum(somador_de_1_bit_4_sum),
    .Carry_Out(somador_de_1_bit_4_carry_out));
  Somador_de_1_bit somador_de_1_bit_5 (
    .A(A4), .B(B4), .Carry_In(somador_de_1_bit_3_carry_out), .Sum(somador_de_1_bit_5_sum),
    .Carry_Out(somador_de_1_bit_5_carry_out));
  Somador_de_1_bit somador_de_1_bit_6 (
    .A(A0), .B(B0), .Carry_In(somador_de_1_bit_4_carry_out), .Sum(somador_de_1_bit_6_sum),
    .Carry_Out(somador_de_1_bit_6_carry_out));
  Somador_de_1_bit somador_de_1_bit_7 (
    .A(A3), .B(B3), .Carry_In(somador_de_1_bit_5_carry_out), .Sum(somador_de_1_bit_7_sum),
    .Carry_Out(somador_de_1_bit_7_carry_out));
  not not_1 (not_1_out, somador_de_1_bit_6_carry_out);
  and and_1 (out_22, not_1_out, somador_de_1_bit_3_sum);
  and and_2 (out_21, not_1_out, somador_de_1_bit_5_sum);
  LED Overflow (.in(somador_de_1_bit_6_carry_out));
  and and_3 (out_20, not_1_out, somador_de_1_bit_7_sum);
  and and_4 (out_19, not_1_out, somador_de_1_bit_2_sum);
  and and_5 (out_18, not_1_out, somador_de_1_bit_4_sum);
  buf and_6 (out_15, not_1_out);  // AND_Gate
  and and_7 (out_17, not_1_out, somador_de_1_bit_6_sum);

  assign out_16 = 1'b0;
endmodule

module Subtrator_de_1_bit (
  input  A,
  input  B,
  input  Borrow_In,
  output Diff,
  output Borrow_Out
);

  wire and_1_out, and_2_out, and_3_out, not_1_out, xor_1_out;

  not not_1 (not_1_out, A);
  and and_1 (and_1_out, B, not_1_out);
  and and_2 (and_2_out, B, Borrow_In);
  and and_3 (and_3_out, not_1_out, Borrow_In);
  xor xor_1 (xor_1_out, A, B);
  xor xor_2 (Diff, xor_1_out, Borrow_In);
  or or_1 (Borrow_Out, and_1_out, and_2_out, and_3_out);
endmodule

module Subtrator_de_8_bits (
  input  in_1,
  input  in_2,
  input  in_3,
  input  in_4,
  input  in_5,
  input  in_6,
  input  in_7,
  input  in_8,
  input  in_9,
  input  in_10,
  input  in_11,
  input  in_12,
  input  in_13,
  input  in_14,
  input  Sinal,
  output out_16,
  output out_17,
  output out_18,
  output out_19,
  output out_20,
  output out_21,
  output out_22,
  output out_23
);

  wire subtrator_de_1_bit_1_borrow_out, subtrator_de_1_bit_2_borrow_out, subtrator_de_1_bit_3_borrow_out,
       subtrator_de_1_bit_4_borrow_out, subtrator_de_1_bit_5_borrow_out, subtrator_de_1_bit_6_borrow_out;

  Subtrator_de_1_bit subtrator_de_1_bit_1 (
    .A(in_2), .B(in_1), .Diff(out_17), .Borrow_Out(subtrator_de_1_bit_1_borrow_out));  // open: Borrow_In
  Subtrator_de_1_bit subtrator_de_1_bit_2 (
    .A(in_4), .B(in_3), .Borrow_In(subtrator_de_1_bit_1_borrow_out), .Diff(out_18),
    .Borrow_Out(subtrator_de_1_bit_2_borrow_out));
  Subtrator_de_1_bit subtrator_de_1_bit_3 (
    .A(in_6), .B(in_5), .Borrow_In(subtrator_de_1_bit_2_borrow_out), .Diff(out_19),
    .Borrow_Out(subtrator_de_1_bit_3_borrow_out));
  Subtrator_de_1_bit subtrator_de_1_bit_4 (
    .A(in_8), .B(in_7), .Borrow_In(subtrator_de_1_bit_3_borrow_out), .Diff(out_20),
    .Borrow_Out(subtrator_de_1_bit_4_borrow_out));
  Subtrator_de_1_bit subtrator_de_1_bit_5 (
    .A(in_10), .B(in_9), .Borrow_In(subtrator_de_1_bit_4_borrow_out), .Diff(out_21),
    .Borrow_Out(subtrator_de_1_bit_5_borrow_out));
  Subtrator_de_1_bit subtrator_de_1_bit_6 (
    .A(in_12), .B(in_11), .Borrow_In(subtrator_de_1_bit_5_borrow_out), .Diff(out_22),
    .Borrow_Out(subtrator_de_1_bit_6_borrow_out));
  Subtrator_de_1_bit subtrator_de_1_bit_7 (
    .A(in_14), .B(in_13), .Borrow_In(subtrator_de_1_bit_6_borrow_out), .Diff(out_23));  // open: Borrow_Out

  assign out_16 = Sinal;
endmodule

// 1
module Comparador_de_igualdade (
  input  A0,
  input  B0,
  input  A1,
  input  B1,
  input  A2,
  input  B2,
  input  A3,
  input  B3,
  input  A4,
  input  B4,
  input  A5,
  input  B5,
  input  A6,
  input  B6,
  input  A7,
  input  B7,
  output out_17
);

  wire and_1_out, and_2_out, and_3_out, and_5_out, and_6_out, and_7_out, xnor_1_out, xnor_2_out, xnor_3_out,
       xnor_4_out, xnor_5_out, xnor_6_out, xnor_7_out, xnor_8_out;

  xnor xnor_1 (xnor_1_out, A0, B0);
  and and_1 (and_1_out, xnor_1_out, xnor_3_out);
  xnor xnor_2 (xnor_2_out, A2, B2);
  xnor xnor_3 (xnor_3_out, A1, B1);
  and and_2 (and_2_out, and_1_out, and_3_out);
  xnor xnor_4 (xnor_4_out, A3, B3);
  and and_3 (and_3_out, xnor_2_out, xnor_4_out);
  and and_4 (out_17, and_2_out, and_6_out);
  xnor xnor_5 (xnor_5_out, A4, B4);
  xnor xnor_6 (xnor_6_out, A5, B5);
  and and_5 (and_5_out, xnor_5_out, xnor_6_out);
  xnor xnor_7 (xnor_7_out, A6, B6);
  and and_6 (and_6_out, and_5_out, and_7_out);
  xnor xnor_8 (xnor_8_out, A7, B7);
  and and_7 (and_7_out, xnor_7_out, xnor_8_out);
endmodule

module Comparador_de_menor_que__8_bits (
  input  A0,
  input  B0,
  input  A1,
  input  B1,
  input  A2,
  input  B2,
  input  A3,
  input  B3,
  input  A4,
  input  B4,
  input  A5,
  input  B5,
  input  A6,
  input  B6,
  input  A7,
  input  B7,
  output out_17
);

  wire and_1_out, and_2_out, and_3_out, and_4_out, and_5_out, and_6_out, and_7_out, and_8_out, and_9_out,
       and_10_out, and_11_out, and_12_out, and_13_out, and_14_out, and_15_out, and_16_out, and_17_out,
       and_18_out, and_19_out, and_20_out, and_21_out, not_1_out, not_2_out, not_3_out, not_4_out, not_5_out,
       not_6_out, not_7_out, not_8_out, or_1_out, or_2_out, or_3_out, or_4_out, or_5_out, or_6_out,
       xnor_1_out, xnor_2_out, xnor_3_out, xnor_4_out, xnor_5_out, xnor_6_out, xnor_7_out;

  not not_1 (not_1_out, A0);
  and and_1 (and_1_out, not_1_out, B0);
  not not_2 (not_2_out, A1);
  xnor xnor_1 (xnor_1_out, A0, B0);
  and and_2 (and_2_out, not_2_out, B1);
  and and_3 (and_3_out, xnor_1_out, and_2_out);
  or or_1 (or_1_out, and_1_out, and_3_out);
  or or_2 (or_2_out, or_1_out, and_6_out);
  not not_3 (not_3_out, A2);
  xnor xnor_2 (xnor_2_out, A1, B1);
  and and_4 (and_4_out, not_3_out, B2);
  and and_5 (and_5_out, xnor_2_out, xnor_1_out);
  and and_6 (and_6_out, and_5_out, and_4_out);
  or or_3 (or_3_out, or_2_out, and_8_out);
  not not_4 (not_4_out, A3);
  xnor xnor_3 (xnor_3_out, A2, B2);
  and and_7 (and_7_out, not_4_out, B3);
  and and_8 (and_8_out, and_9_out, and_7_out);
  and and_9 (and_9_out, xnor_3_out, and_5_out);
  and and_10 (and_10_out, xnor_4_out, and_9_out);
  or or_4 (or_4_out, or_3_out, and_11_out);
  and and_11 (and_11_out, and_10_out, and_12_out);
  or or_5 (or_5_out, or_4_out, and_14_out);
  xnor xnor_4 (xnor_4_out, A3, B3);
  not not_5 (not_5_out, A4);
  and and_12 (and_12_out, not_5_out, B4);
  not not_6 (not_6_out, A5);
  and and_13 (and_13_out, xnor_5_out, and_10_out);
  and and_14 (and_14_out, and_13_out, and_15_out);
  or or_6 (or_6_out, or_5_out, and_18_out);
  xnor xnor_5 (xnor_5_out, A4, B4);
  and and_15 (and_15_out, not_6_out, B5);
  not not_7 (not_7_out, A6);
  and and_16 (and_16_out, not_7_out, B6);
  and and_17 (and_17_out, xnor_6_out, and_13_out);
  and and_18 (and_18_out, and_17_out, and_16_out);
  or or_7 (out_17, or_6_out, and_20_out);
  xnor xnor_6 (xnor_6_out, A5, B5);
  and and_19 (and_19_out, xnor_7_out, and_17_out);
  and and_20 (and_20_out, and_19_out, and_21_out);
  xnor xnor_7 (xnor_7_out, A6, B6);
  not not_8 (not_8_out, A7);
  and and_21 (and_21_out, not_8_out, B7);
endmodule

module Comparador_de_maior_que__8_bits (
  input  A0,
  input  B0,
  input  A1,
  input  B1,
  input  A2,
  input  B2,
  input  A3,
  input  B3,
  input  A4,
  input  B4,
  input  A5,
  input  B5,
  input  A6,
  input  B6,
  input  A7,
  input  B8,
  output out_17
);

  wire and_1_out, and_2_out, and_3_out, and_4_out, and_5_out, and_6_out, and_7_out, and_8_out, and_9_out,
       and_10_out, and_11_out, and_12_out, and_13_out, and_14_out, and_15_out, and_16_out, and_17_out,
       and_18_out, and_19_out, and_20_out, and_22_out, and_23_out, not_1_out, not_2_out, not_3_out,
       not_4_out, not_5_out, not_6_out, not_7_out, not_8_out, not_9_out, not_10_out, or_1_out, or_2_out,
       or_3_out, or_4_out, or_5_out, or_6_out, or_7_out, xnor_1_out, xnor_2_out, xnor_3_out, xnor_4_out,
       xnor_5_out, xnor_6_out, xnor_7_out, xnor_8_out;

  not not_1 (not_1_out, A0);
  and and_1 (and_1_out, not_1_out, B0);
  not not_2 (not_2_out, A1);
  xnor xnor_1 (xnor_1_out, A0, B0);
  and and_2 (and_2_out, not_2_out, B1);
  and and_3 (and_3_out, xnor_1_out, and_2_out);
  or or_1 (or_1_out, and_1_out, and_3_out);
  or or_2 (or_2_out, or_1_out, and_6_out);
  not not_3 (not_3_out, A2);
  xnor xnor_2 (xnor_2_out, A1, B1);
  and and_4 (and_4_out, not_3_out, B2);
  and and_5 (and_5_out, xnor_2_out, xnor_1_out);
  and and_6 (and_6_out, and_5_out, and_4_out);
  or or_3 (or_3_out, or_2_out, and_8_out);
  not not_4 (not_4_out, A3);
  and and_7 (and_7_out, not_4_out, B3);
  xnor xnor_3 (xnor_3_out, A2, B2);
  and and_8 (and_8_out, and_9_out, and_7_out);
  and and_9 (and_9_out, xnor_3_out, and_5_out);
  and and_10 (and_10_out, xnor_4_out, and_9_out);
  or or_4 (or_4_out, or_3_out, and_11_out);
  and and_11 (and_11_out, and_10_out, and_12_out);
  or or_5 (or_5_out, or_4_out, and_14_out);
  xnor xnor_4 (xnor_4_out, A3, B3);
  not not_5 (not_5_out, A4);
  and and_12 (and_12_out, not_5_out, B4);
  not not_6 (not_6_out, A5);
  and and_13 (and_13_out, xnor_5_out, and_10_out);
  and and_14 (and_14_out, and_13_out, and_15_out);
  or or_6 (or_6_out, or_5_out, and_18_out);
  xnor xnor_5 (xnor_5_out, A4, B4);
  and and_15 (and_15_out, not_6_out, B5);
  not not_7 (not_7_out, A6);
  and and_16 (and_16_out, not_7_out, B6);
  and and_17 (and_17_out, xnor_6_out, and_13_out);
  and and_18 (and_18_out, and_17_out, and_16_out);
  or or_7 (or_7_out, or_6_out, and_20_out);
  not not_8 (not_8_out, or_7_out);
  xnor xnor_6 (xnor_6_out, A5, B5);
  and and_19 (and_19_out, xnor_7_out, and_17_out);
  and and_20 (and_20_out, and_19_out, and_22_out);
  and and_21 (out_17, not_8_out, not_10_out);
  xnor xnor_7 (xnor_7_out, A6, B6);
  not not_9 (not_9_out, A7);
  and and_22 (and_22_out, not_9_out, B8);
  and and_23 (and_23_out, xnor_8_out, and_19_out);
  not not_10 (not_10_out, and_23_out);
  xnor xnor_8 (xnor_8_out, A7, B8);
endmodule
