// Logisim project ULA.circ as structural Verilog: 11 circuits, main circuit main
module main (
  input  A_0,
  input  B_0,
  input  A_1,
  input  B_1,
  input  A_2,
  input  B_2,
  input  A_3,
  input  B_3,
  input  A_4,
  input  B_4,
  input  A_5,
  input  B_5,
  input  A_6,
  input  B_6,
  input  A_7,
  input  B_7,
  input  X,
  input  Y,
  input  Z,
  output out_20,
  output out_21,
  output out_22,
  output out_23,
  output out_24,
  output out_25,
  output out_26,
  output out_27,
  output out_28,
  output out_29,
  output out_30,
  output out_31,
  output out_32,
  output out_33,
  output out_34,
  output out_35,
  output out_36,
  output out_37,
  output out_38,
  output out_39,
  output out_40,
  output out_41,
  output out_42,
  output out_43,
  output out_44,
  output out_45,
  output out_46,
  output out_47,
  output out_48,
  output out_49,
  output out_50,
  output out_51,
  output out_52,
  output out_53,
  output out_54,
  output out_55,
  output out_56,
  output out_57,
  output out_58,
  output out_59
);

  wire and_1_out, and_2_out, and_3_out, and_4_out, and_5_out, and_6_out, and_7_out, and_8_out,
       comp_igual_8_bits_1_out_18, comp_maior_0_8_bits_1_out_18, comp_menor_0_8_bits_1_out_18, not_1_out,
       not_2_out, not_3_out, not_4_out, not_5_out, not_6_out, not_7_out, not_8_out, not_9_out, not_10_out,
       not_11_out, not_12_out;

  not not_1 (not_1_out, X);
  not not_2 (not_2_out, Y);
  not not_3 (not_3_out, Z);
  not not_4 (not_4_out, X);
  not not_5 (not_5_out, Y);
  not not_6 (not_6_out, X);
  not not_7 (not_7_out, Z);
  not not_8 (not_8_out, X);
  not not_9 (not_9_out, Y);
  not not_10 (not_10_out, Z);
  not not_11 (not_11_out, Y);
  not not_12 (not_12_out, Z);
  and and_1 (and_1_out, not_1_out, not_2_out, not_3_out);
  and and_2 (and_2_out, not_4_out, not_5_out, Z);
  and and_3 (and_3_out, not_6_out, Y, not_7_out);
  and and_4 (and_4_out, not_8_out, Y, Z);
  and and_5 (and_5_out, X, not_9_out, not_10_out);
  and and_6 (and_6_out, X, not_11_out, Z);
  and and_7 (and_7_out, X, Y, not_12_out);
  and and_8 (and_8_out, X, Y, Z);
  Sum_8_bits sum_8_bits_1 (
    .A_1(A_1), .A_2(A_2), .A_3(A_3), .A_4(A_4), .A_5(A_5), .A_6(A_6), .A_7(A_7), .Chave(and_1_out),
    .B_1(B_1), .B_2(B_2), .B_3(B_3), .B_4(B_4), .B_5(B_5), .B_6(B_6), .B_7(B_7), .out_16(out_20),
    .out_17(out_21), .out_18(out_22), .out_19(out_23), .out_20(out_24), .out_21(out_25), .out_22(out_26),
    .out_23(out_27));
  Sub_8_bits sub_8_bits_1 (
    .A_1(A_1), .A_2(A_2), .A_3(A_3), .A_4(A_4), .A_5(A_5), .A_6(A_6), .A_7(A_7), .Chave(and_2_out),
    .B_1(B_1), .B_2(B_2), .B_3(B_3), .B_4(B_4), .B_5(B_5), .B_6(B_6), .B_7(B_7), .out_16(out_28),
    .out_17(out_29), .out_18(out_30), .out_19(out_31), .out_20(out_32), .out_21(out_33), .out_22(out_34),
    .out_23(out_35));
  Not_8_bits not_8_bits_1 (
    .A_0(A_0), .A_1(A_1), .A_2(A_2), .A_3(A_3), .A_4(A_4), .A_5(A_5), .A_6(A_6), .A_7(A_7), .out_10(out_36),
    .out_11(out_37), .out_12(out_38), .out_13(out_39), .out_14(out_40), .out_15(out_41), .out_16(out_42),
    .out_17(out_43), .Chave(and_3_out));
  And_8_bits and_8_bits_1 (
    .A_0(A_0), .A_1(A_1), .A_2(A_2), .A_3(A_3), .A_4(A_4), .A_5(A_5), .A_6(A_6), .A_7(A_7), .B_0(B_0),
    .B_1(B_1), .B_2(B_2), .B_3(B_3), .B_4(B_4), .B_5(B_5), .B_6(B_6), .B_7(B_7), .Chave(and_4_out),
    .out_18(out_44), .out_19(out_45), .out_20(out_46), .out_21(out_47), .out_22(out_48), .out_23(out_49),
    .out_24(out_50), .out_25(out_51));
  Or_8_bits or_8_bits_1 (
    .A_0(A_0), .A_1(A_1), .A_2(A_2), .A_3(A_3), .A_4(A_4), .A_5(A_5), .A_6(A_6), .A_7(A_7),
    .Chave(and_5_out), .B_0(B_0), .B_1(B_1), .B_2(B_2), .B_3(B_3), .B_4(B_4), .B_5(B_5), .B_6(B_6),
    .B_7(B_7), .out_18(out_52), .out_19(out_53), .out_20(out_54), .out_21(out_55), .out_22(out_56),
    .out_23(out_57), .out_24(out_58), .out_25(out_59));
  Comp_Igual_8_bits comp_igual_8_bits_1 (
    .A_0(A_0), .A_1(A_1), .A_2(A_2), .A_3(A_3), .Chave(and_6_out), .A_4(A_4), .A_5(A_5), .A_6(A_6),
    .A_7(A_7), .out_18(comp_igual_8_bits_1_out_18), .B_0(B_0), .B_1(B_1), .B_2(B_2), .B_3(B_3), .B_4(B_4),
    .B_5(B_5), .B_6(B_6), .B_7(B_7));
  LED Iguais (.in(comp_igual_8_bits_1_out_18));
  Comp_Menor_0__8_bits comp_menor_0_8_bits_1 (
    .A5(A_5), .B5(B_5), .A6(A_6), .B6(B_6), .A7(A_7), .B7(B_7), .A0(A_0), .B0(B_0), .A1(A_1), .B1(B_1),
    .A2(A_2), .B2(B_2), .A3(A_3), .B3(B_3), .A4(A_4), .B4(B_4), .out_18(comp_menor_0_8_bits_1_out_18),
    .Chave(and_7_out));
  LED A___B (.in(comp_menor_0_8_bits_1_out_18));
  Comp_Maior_0__8_bits comp_maior_0_8_bits_1 (
    .B5(B_5), .A5(A_5), .B6(B_6), .A6(A_6), .B7(B_7), .A7(A_7), .B0(B_0), .A0(A_0), .B1(B_1), .A1(A_1),
    .B2(B_2), .A2(A_2), .B3(B_3), .B4(B_4), .Chave(and_8_out), .out_18(comp_maior_0_8_bits_1_out_18),
    .A3(A_3), .A4(A_4));
  LED A___B_2 (.in(comp_maior_0_8_bits_1_out_18));

  // Notes on the sheet:
  //   SUM
  //   SUB
  //   NOT
  //   AND
  //   OR
  //   Comp Igual
  //   Comp Menor
  //   Comp Maior
endmodule

module Sum_1_bit (
  input  A,
  input  B,
  input  Carry_In,
  output Output,
  output Carry_Out
);

  wire and_1_out, and_2_out, and_3_out, xor_1_out;

  xor xor_1 (xor_1_out, A, B);
  and and_1 (and_1_out, A, B);
  and and_2 (and_2_out, A, Carry_In);
  and and_3 (and_3_out, B, Carry_In);
  xor xor_2 (Output, xor_1_out, Carry_In);
  or or_1 (Carry_Out, and_1_out, and_2_out, and_3_out);
endmodule

module Sum_8_bits (
  input  B_1,
  input  B_2,
  input  B_3,
  input  B_4,
  input  B_5,
  input  B_6,
  input  B_7,
  input  A_1,
  input  A_2,
  input  A_3,
  input  A_4,
  input  A_5,
  input  A_6,
  input  A_7,
  input  Chave,
  output out_16,
  output out_17,
  output out_18,
  output out_19,
  output out_20,
  output out_21,
  output out_22,
  output out_23
);

  wire not_1_out, sum_1_bit_1_carry_out, sum_1_bit_1_output, sum_1_bit_2_carry_out, sum_1_bit_2_output,
       sum_1_bit_3_carry_out, sum_1_bit_3_output, sum_1_bit_4_carry_out, sum_1_bit_4_output,
       sum_1_bit_5_carry_out, sum_1_bit_5_output, sum_1_bit_6_carry_out, sum_1_bit_6_output,
       sum_1_bit_7_carry_out, sum_1_bit_7_output;

  Sum_1_bit sum_1_bit_1 (
    .A(A_7), .B(B_7), .Carry_In(1'b0), .Output(sum_1_bit_1_output), .Carry_Out(sum_1_bit_1_carry_out));
  Sum_1_bit sum_1_bit_2 (
    .A(A_6), .B(B_6), .Carry_In(sum_1_bit_1_carry_out), .Output(sum_1_bit_2_output),
    .Carry_Out(sum_1_bit_2_carry_out));
  Sum_1_bit sum_1_bit_3 (
    .A(A_5), .B(B_5), .Carry_In(sum_1_bit_2_carry_out), .Output(sum_1_bit_3_output),
    .Carry_Out(sum_1_bit_3_carry_out));
  Sum_1_bit sum_1_bit_4 (
    .A(A_4), .B(B_4), .Carry_In(sum_1_bit_3_carry_out), .Output(sum_1_bit_4_output),
    .Carry_Out(sum_1_bit_4_carry_out));
  Sum_1_bit sum_1_bit_5 (
    .A(A_3), .B(B_3), .Carry_In(sum_1_bit_4_carry_out), .Output(sum_1_bit_5_output),
    .Carry_Out(sum_1_bit_5_carry_out));
  Sum_1_bit sum_1_bit_6 (
    .A(A_2), .B(B_2), .Carry_In(sum_1_bit_5_carry_out), .Output(sum_1_bit_6_output),
    .Carry_Out(sum_1_bit_6_carry_out));
  Sum_1_bit sum_1_bit_7 (
    .A(A_1), .B(B_1), .Carry_In(sum_1_bit_6_carry_out), .Output(sum_1_bit_7_output),
    .Carry_Out(sum_1_bit_7_carry_out));
  not not_1 (not_1_out, sum_1_bit_7_carry_out);
  LED Overflow (.in(sum_1_bit_7_carry_out));
  and and_1 (out_17, sum_1_bit_7_output, Chave, not_1_out);
  and and_2 (out_18, sum_1_bit_6_output, Chave, not_1_out);
  and and_3 (out_19, sum_1_bit_5_output, Chave, not_1_out);
  and and_4 (out_20, sum_1_bit_4_output, Chave, not_1_out);
  and and_5 (out_21, sum_1_bit_3_output, Chave, not_1_out);
  and and_6 (out_23, sum_1_bit_1_output, Chave, not_1_out);
  and and_7 (out_22, sum_1_bit_2_output, Chave, not_1_out);

  assign out_16 = 1'b0;
endmodule

module Sub_1_bit (
  input  A,
  input  B,
  input  Borrow_In,
  output Output,
  output Borrow_Out
);

  wire and_1_out, and_2_out, and_3_out, not_1_out, xor_1_out;

  not not_1 (not_1_out, A);
  xor xor_1 (xor_1_out, A, B);
  and and_1 (and_1_out, not_1_out, B);
  and and_2 (and_2_out, not_1_out, Borrow_In);
  and and_3 (and_3_out, B, Borrow_In);
  xor xor_2 (Output, xor_1_out, Borrow_In);
  or or_1 (Borrow_Out, and_1_out, and_2_out, and_3_out);
endmodule

module Sub_8_bits (
  input  B_1,
  input  B_2,
  input  B_3,
  input  B_4,
  input  B_5,
  input  B_6,
  input  B_7,
  input  A_1,
  input  A_2,
  input  A_3,
  input  A_4,
  input  A_5,
  input  A_6,
  input  A_7,
  input  Chave,
  output out_16,
  output out_17,
  output out_18,
  output out_19,
  output out_20,
  output out_21,
  output out_22,
  output out_23
);

  wire sub_1_bit_1_borrow_out, sub_1_bit_1_output, sub_1_bit_2_borrow_out, sub_1_bit_2_output,
       sub_1_bit_3_borrow_out, sub_1_bit_3_output, sub_1_bit_4_borrow_out, sub_1_bit_4_output,
       sub_1_bit_5_borrow_out, sub_1_bit_5_output, sub_1_bit_6_borrow_out, sub_1_bit_6_output,
       sub_1_bit_7_borrow_out, sub_1_bit_7_output, sum_8_bits_1_out_17, sum_8_bits_1_out_18,
       sum_8_bits_1_out_19, sum_8_bits_1_out_20, sum_8_bits_1_out_21, sum_8_bits_1_out_22,
       sum_8_bits_1_out_23, xor_1_out, xor_2_out, xor_3_out, xor_4_out, xor_5_out, xor_6_out, xor_7_out;

  and and_1 (out_16, sub_1_bit_7_borrow_out, Chave);
  and and_2 (out_17, sum_8_bits_1_out_17, Chave);
  Sub_1_bit sub_1_bit_1 (
    .A(A_7), .B(B_7), .Borrow_In(1'b0), .Output(sub_1_bit_1_output), .Borrow_Out(sub_1_bit_1_borrow_out));
  Sub_1_bit sub_1_bit_2 (
    .A(A_6), .B(B_6), .Borrow_In(sub_1_bit_1_borrow_out), .Output(sub_1_bit_2_output),
    .Borrow_Out(sub_1_bit_2_borrow_out));
  Sub_1_bit sub_1_bit_3 (
    .A(A_5), .B(B_5), .Borrow_In(sub_1_bit_2_borrow_out), .Output(sub_1_bit_3_output),
    .Borrow_Out(sub_1_bit_3_borrow_out));
  Sub_1_bit sub_1_bit_4 (
    .A(A_4), .B(B_4), .Borrow_In(sub_1_bit_3_borrow_out), .Output(sub_1_bit_4_output),
    .Borrow_Out(sub_1_bit_4_borrow_out));
  Sub_1_bit sub_1_bit_5 (
    .A(A_3), .B(B_3), .Borrow_In(sub_1_bit_4_borrow_out), .Output(sub_1_bit_5_output),
    .Borrow_Out(sub_1_bit_5_borrow_out));
  Sub_1_bit sub_1_bit_6 (
    .A(A_2), .B(B_2), .Borrow_In(sub_1_bit_5_borrow_out), .Output(sub_1_bit_6_output),
    .Borrow_Out(sub_1_bit_6_borrow_out));
  Sub_1_bit sub_1_bit_7 (
    .A(A_1), .B(B_1), .Borrow_In(sub_1_bit_6_borrow_out), .Output(sub_1_bit_7_output),
    .Borrow_Out(sub_1_bit_7_borrow_out));
  Sum_8_bits sum_8_bits_1 (
    .A_1(xor_1_out), .A_2(xor_3_out), .A_3(xor_2_out), .A_4(xor_4_out), .A_5(xor_5_out), .A_6(xor_7_out),
    .A_7(xor_6_out), .Chave(1'b1), .B_1(1'b0), .B_2(1'b0), .B_3(1'b0), .B_4(1'b0), .B_5(1'b0), .B_6(1'b0),
    .B_7(sub_1_bit_7_borrow_out), .out_17(sum_8_bits_1_out_17), .out_18(sum_8_bits_1_out_18),
    .out_19(sum_8_bits_1_out_19), .out_20(sum_8_bits_1_out_20), .out_21(sum_8_bits_1_out_21),
    .out_22(sum_8_bits_1_out_22), .out_23(sum_8_bits_1_out_23));  // open: out_16
  and and_3 (out_18, sum_8_bits_1_out_18, Chave);
  and and_4 (out_19, sum_8_bits_1_out_19, Chave);
  and and_5 (out_20, sum_8_bits_1_out_20, Chave);
  xor xor_1 (xor_1_out, sub_1_bit_7_output, sub_1_bit_7_borrow_out);
  and and_6 (out_21, sum_8_bits_1_out_21, Chave);
  and and_7 (out_22, sum_8_bits_1_out_22, Chave);
  xor xor_2 (xor_2_out, sub_1_bit_5_output, sub_1_bit_7_borrow_out);
  xor xor_3 (xor_3_out, sub_1_bit_6_output, sub_1_bit_7_borrow_out);
  and and_8 (out_23, sum_8_bits_1_out_23, Chave);
  xor xor_4 (xor_4_out, sub_1_bit_4_output, sub_1_bit_7_borrow_out);
  xor xor_5 (xor_5_out, sub_1_bit_3_output, sub_1_bit_7_borrow_out);
  xor xor_6 (xor_6_out, sub_1_bit_1_output, sub_1_bit_7_borrow_out);
  xor xor_7 (xor_7_out, sub_1_bit_2_output, sub_1_bit_7_borrow_out);
endmodule

module Not_8_bits (
  input  Chave,
  input  A_0,
  input  A_1,
  input  A_2,
  input  A_3,
  input  A_4,
  input  A_5,
  input  A_6,
  input  A_7,
  output out_10,
  output out_11,
  output out_12,
  output out_13,
  output out_14,
  output out_15,
  output out_16,
  output out_17
);

  wire not_1_out, not_2_out, not_3_out, not_4_out, not_5_out, not_6_out, not_7_out, not_8_out;

  not not_1 (not_1_out, A_0);
  not not_2 (not_2_out, A_1);
  not not_3 (not_3_out, A_2);
  not not_4 (not_4_out, A_3);
  not not_5 (not_5_out, A_4);
  not not_6 (not_6_out, A_5);
  not not_7 (not_7_out, A_6);
  not not_8 (not_8_out, A_7);
  and and_1 (out_10, not_1_out, Chave);
  and and_2 (out_11, not_2_out, Chave);
  and and_3 (out_12, not_3_out, Chave);
  and and_4 (out_13, not_4_out, Chave);
  and and_5 (out_14, not_5_out, Chave);
  and and_6 (out_15, not_6_out, Chave);
  and and_7 (out_16, not_7_out, Chave);
  and and_8 (out_17, not_8_out, Chave);
endmodule

module And_8_bits (
  input  Chave,
  input  B_0,
  input  B_1,
  input  B_2,
  input  B_3,
  input  B_4,
  input  B_5,
  input  B_6,
  input  B_7,
  input  A_0,
  input  A_1,
  input  A_2,
  input  A_3,
  input  A_4,
  input  A_5,
  input  A_6,
  input  A_7,
  output out_18,
  output out_19,
  output out_20,
  output out_21,
  output out_22,
  output out_23,
  output out_24,
  output out_25
);

  and and_1 (out_18, B_0, Chave, A_0);
  and and_2 (out_19, B_1, Chave, A_1);
  and and_3 (out_20, B_2, Chave, A_2);
  and and_4 (out_21, B_3, Chave, A_3);
  and and_5 (out_22, B_4, Chave, A_4);
  and and_6 (out_23, B_5, Chave, A_5);
  and and_7 (out_24, B_6, Chave, A_6);
  and and_8 (out_25, B_7, Chave, A_7);
endmodule

module Or_8_bits (
  input  B_0,
  input  B_1,
  input  B_2,
  input  B_3,
  input  B_4,
  input  B_5,
  input  B_6,
  input  B_7,
  input  A_0,
  input  A_1,
  input  A_2,
  input  A_3,
  input  A_4,
  input  A_5,
  input  A_6,
  input  A_7,
  input  Chave,
  output out_18,
  output out_19,
  output out_20,
  output out_21,
  output out_22,
  output out_23,
  output out_24,
  output out_25
);

  wire or_1_out, or_2_out, or_3_out, or_4_out, or_5_out, or_6_out, or_7_out, or_8_out;

  or or_1 (or_1_out, B_0, A_0);
  or or_2 (or_2_out, B_1, A_1);
  or or_3 (or_3_out, B_2, A_2);
  or or_4 (or_4_out, B_3, A_3);
  or or_5 (or_5_out, B_4, A_4);
  or or_6 (or_6_out, B_5, A_5);
  or or_7 (or_7_out, B_6, A_6);
  or or_8 (or_8_out, B_7, A_7);
  and and_1 (out_18, or_1_out, Chave);
  and and_2 (out_19, or_2_out, Chave);
  and and_3 (out_21, or_4_out, Chave);
  and and_4 (out_20, or_3_out, Chave);
  and and_5 (out_22, or_5_out, Chave);
  and and_6 (out_23, or_6_out, Chave);
  and and_7 (out_24, or_7_out, Chave);
  and and_8 (out_25, or_8_out, Chave);
endmodule

module Comp_Igual_8_bits (
  input  B_0,
  input  B_1,
  input  B_2,
  input  B_3,
  input  B_4,
  input  B_5,
  input  B_6,
  input  B_7,
  input  A_0,
  input  A_1,
  input  A_2,
  input  A_3,
  input  Chave,
  input  A_4,
  input  A_5,
  input  A_6,
  input  A_7,
  output out_18
);

  wire and_1_out, and_2_out, xnor_1_out, xnor_2_out, xnor_3_out, xnor_4_out, xnor_5_out, xnor_6_out,
       xnor_7_out, xnor_8_out;

  xnor xnor_1 (xnor_1_out, B_0, A_0);
  xnor xnor_2 (xnor_2_out, B_1, A_1);
  xnor xnor_3 (xnor_3_out, B_2, A_2);
  xnor xnor_4 (xnor_4_out, B_3, A_3);
  xnor xnor_5 (xnor_5_out, B_4, A_4);
  xnor xnor_6 (xnor_6_out, B_5, A_5);
  xnor xnor_7 (xnor_7_out, B_6, A_6);
  xnor xnor_8 (xnor_8_out, B_7, A_7);
  and and_1 (and_1_out, xnor_1_out, xnor_2_out, xnor_3_out, xnor_4_out);
  and and_2 (and_2_out, xnor_5_out, xnor_6_out, xnor_7_out, xnor_8_out);
  and and_3 (out_18, and_1_out, Chave, and_2_out);
endmodule

module Comp_Menor_0__8_bits (
  input  A0,
  input  B0,
  input  A1,
  input  B1,
  input  A2,
  input  B2,
  input  A3,
  input  B3,
  input  A4,
  input  B4,
  input  A5,
  input  B5,
  input  A6,
  input  B6,
  input  A7,
  input  B7,
  input  Chave,
  output out_18
);

  wire and_1_out, and_2_out, and_3_out, and_4_out, and_5_out, and_6_out, and_7_out, and_8_out, and_9_out,
       and_10_out, and_11_out, and_12_out, and_13_out, and_14_out, and_15_out, and_16_out, and_17_out,
       and_18_out, and_20_out, and_21_out, and_22_out, not_1_out, not_2_out, not_3_out, not_4_out, not_5_out,
       not_6_out, not_7_out, not_8_out, or_1_out, or_2_out, or_3_out, or_4_out, or_5_out, or_6_out, or_7_out,
       xnor_1_out, xnor_2_out, xnor_3_out, xnor_4_out, xnor_5_out, xnor_6_out, xnor_7_out;

  not not_1 (not_1_out, A0);
  and and_1 (and_1_out, not_1_out, B0);
  not not_2 (not_2_out, A1);
  xnor xnor_1 (xnor_1_out, A0, B0);
  and and_2 (and_2_out, not_2_out, B1);
  and and_3 (and_3_out, xnor_1_out, and_2_out);
  or or_1 (or_1_out, and_1_out, and_3_out);
  or or_2 (or_2_out, or_1_out, and_6_out);
  not not_3 (not_3_out, A2);
  xnor xnor_2 (xnor_2_out, A1, B1);
  and and_4 (and_4_out, not_3_out, B2);
  and and_5 (and_5_out, xnor_2_out, xnor_1_out);
  and and_6 (and_6_out, and_5_out, and_4_out);
  or or_3 (or_3_out, or_2_out, and_8_out);
  not not_4 (not_4_out, A3);
  xnor xnor_3 (xnor_3_out, A2, B2);
  and and_7 (and_7_out, not_4_out, B3);
  and and_8 (and_8_out, and_9_out, and_7_out);
  and and_9 (and_9_out, xnor_3_out, and_5_out);
  and and_10 (and_10_out, xnor_4_out, and_9_out);
  or or_4 (or_4_out, or_3_out, and_11_out);
  and and_11 (and_11_out, and_10_out, and_12_out);
  or or_5 (or_5_out, or_4_out, and_14_out);
  xnor xnor_4 (xnor_4_out, A3, B3);
  not not_5 (not_5_out, A4);
  and and_12 (and_12_out, not_5_out, B4);
  not not_6 (not_6_out, A5);
  and and_13 (and_13_out, xnor_5_out, and_10_out);
  and and_14 (and_14_out, and_13_out, and_15_out);
  or or_6 (or_6_out, or_5_out, and_18_out);
  xnor xnor_5 (xnor_5_out, A4, B4);
  and and_15 (and_15_out, not_6_out, B5);
  not not_7 (not_7_out, A6);
  and and_16 (and_16_out, not_7_out, B6);
  and and_17 (and_17_out, xnor_6_out, and_13_out);
  and and_18 (and_18_out, and_17_out, and_16_out);
  or or_7 (or_7_out, or_6_out, and_21_out);
  and and_19 (out_18, Chave, or_7_out);
  xnor xnor_6 (xnor_6_out, A5, B5);
  and and_20 (and_20_out, xnor_7_out, and_17_out);
  and and_21 (and_21_out, and_20_out, and_22_out);
  xnor xnor_7 (xnor_7_out, A6, B6);
  not not_8 (not_8_out, A7);
  and and_22 (and_22_out, not_8_out, B7);
endmodule

module Comp_Maior_0__8_bits (
  input  B0,
  input  A0,
  input  B1,
  input  A1,
  input  B2,
  input  A2,
  input  B3,
  input  A3,
  input  B4,
  input  A4,
  input  B5,
  input  A5,
  input  B6,
  input  A6,
  input  B7,
  input  A7,
  input  Chave,
  output out_18
);

  wire and_1_out, and_2_out, and_3_out, and_4_out, and_5_out, and_6_out, and_7_out, and_8_out, and_9_out,
       and_10_out, and_11_out, and_12_out, and_13_out, and_14_out, and_15_out, and_16_out, and_17_out,
       and_18_out, and_20_out, and_21_out, and_22_out, not_1_out, not_2_out, not_3_out, not_4_out, not_5_out,
       not_6_out, not_7_out, not_8_out, or_1_out, or_2_out, or_3_out, or_4_out, or_5_out, or_6_out, or_7_out,
       xnor_1_out, xnor_2_out, xnor_3_out, xnor_4_out, xnor_5_out, xnor_6_out, xnor_7_out;

  not not_1 (not_1_out, B0);
  and and_1 (and_1_out, not_1_out, A0);
  not not_2 (not_2_out, B1);
  xnor xnor_1 (xnor_1_out, B0, A0);
  and and_2 (and_2_out, not_2_out, A1);
  and and_3 (and_3_out, xnor_1_out, and_2_out);
  or or_1 (or_1_out, and_1_out, and_3_out);
  or or_2 (or_2_out, or_1_out, and_6_out);
  not not_3 (not_3_out, B2);
  xnor xnor_2 (xnor_2_out, B1, A1);
  and and_4 (and_4_out, not_3_out, A2);
  and and_5 (and_5_out, xnor_2_out, xnor_1_out);
  and and_6 (and_6_out, and_5_out, and_4_out);
  or or_3 (or_3_out, or_2_out, and_8_out);
  not not_4 (not_4_out, B3);
  xnor xnor_3 (xnor_3_out, B2, A2);
  and and_7 (and_7_out, not_4_out, A3);
  and and_8 (and_8_out, and_9_out, and_7_out);
  and and_9 (and_9_out, xnor_3_out, and_5_out);
  and and_10 (and_10_out, xnor_4_out, and_9_out);
  or or_4 (or_4_out, or_3_out, and_11_out);
  and and_11 (and_11_out, and_10_out, and_12_out);
  or or_5 (or_5_out, or_4_out, and_14_out);
  xnor xnor_4 (xnor_4_out, B3, A3);
  not not_5 (not_5_out, B4);
  and and_12 (and_12_out, not_5_out, A4);
  not not_6 (not_6_out, B5);
  and and_13 (and_13_out, xnor_5_out, and_10_out);
  and and_14 (and_14_out, and_13_out, and_15_out);
  or or_6 (or_6_out, or_5_out, and_18_out);
  xnor xnor_5 (xnor_5_out, B4, A4);
  and and_15 (and_15_out, not_6_out, A5);
  not not_7 (not_7_out, B6);
  and and_16 (and_16_out, not_7_out, A6);
  and and_17 (and_17_out, xnor_6_out, and_13_out);
  and and_18 (and_18_out, and_17_out, and_16_out);
  or or_7 (or_7_out, or_6_out, and_21_out);
  and and_19 (out_18, Chave, or_7_out);
  xnor xnor_6 (xnor_6_out, B5, A5);
  and and_20 (and_20_out, xnor_7_out, and_17_out);
  and and_21 (and_21_out, and_20_out, and_22_out);
  xnor xnor_7 (xnor_7_out, B6, A6);
  not not_8 (not_8_out, B7);
  and and_22 (and_22_out, not_8_out, A7);
endmodule
